# Fritzing sketch ex03 (saved by Fritzing 0.9.3b)
breadboards: 1

parts:
  元件1 = Arduino Nano (Rev3.0)
  R1 = Photocell (LDR) [package=THT]
  R2 = Temperature Sensor (Thermistor) [thermistor_type=NTC package=THT]
  R3 = Resistor [tolerance=±20% resistance=10k package=THT]
  R4 = Resistor [tolerance=±20% resistance=10k package=THT]
  LED1 = LED - 3mm [color="Red (635nm)" package="3 mm [THT]"]
  LED2 = LED - 3mm [color="Orange (620nm)" package="3 mm [THT]"]
  R5 = Resistor [tolerance=±20% resistance=470 package=THT]
  R6 = Resistor [tolerance=±20% resistance=470 package=THT]
  R7 = Resistor [tolerance=±20% resistance=470 package=THT]
  R8 = Resistor [tolerance=±20% resistance=470 package=THT]
  R9 = Resistor [tolerance=±20% resistance=470 package=THT]
  LED3 = LED - 3mm [color="Yellow (595nm)" package="3 mm [THT]"]
  LED4 = LED - 3mm [color="Green (570nm)" package="3 mm [THT]"]
  LED5 = LED - 3mm [color="Blue (525nm)" package="3 mm [THT]"]

nets:
  N1: 元件1.GND, R3.Pin_0, R4.Pin_0
  N2: 元件1.D3, R9.Pin_0
  N3: 元件1.D5, R8.Pin_0
  N4: 元件1.D6, R7.Pin_0
  N5: 元件1.D9, R6.Pin_0
  N6: 元件1.D10, R5.Pin_0
  N7: 元件1.5V, 元件1.A1, 元件1.A0, R1.pin_0, R1.pin_1, R2.pin_0, R2.pin_1, R3.Pin_1, R4.Pin_1, LED1.cathode, LED1.anode, LED2.cathode, LED2.anode, R5.Pin_1, R6.Pin_1, R7.Pin_1, R8.Pin_1, R9.Pin_1, LED3.cathode, LED3.anode, LED4.cathode, LED4.anode, LED5.cathode, LED5.anode
